# Fritzing sketch Asset (saved by Fritzing 0.9.3b)

parts:
  U1 = NodeMCU V1.0
  Part1 = Adafruit RFM69HCW Transceiver Radio [part_number="Adafruit #3070 and #3071"]
  BAT1 = CR123 battery holder [package=battery-18650-kit]
  A1 = u-blox NEO-6M GPS Breakout
  A2 = ESP32 UWB v1.0  # not connected

nets:
  N1: U1.D0, Part1.RST
  N2: U1.D1, Part1.DIO0
  N3: U1.D2, A1.Pin_4
  N4: U1.D3, A1.Pin_3
  GND: U1.GND, Part1.GND, BAT1.-, A1.Pin_2
  N5: U1.D5, Part1.SCK
  N6: U1.D6, Part1.MISO
  N7: U1.D7, Part1.MOSI
  N8: U1.D8, Part1.CS
  VIN: U1.Vin, Part1.VIN, BAT1.+, A1.Pin_1

custom parts:
  NodeMCU V1.0: ESP8266 based NodeMCU
  Adafruit RFM69HCW Transceiver Radio: Sending data over long distances is like magic, and now you can be a magician with this range of powerful and easy-to-use radio modules. Sure, sometimes you want to talk to a computer (a good time to use WiFi) or perhaps communicate with a Phone (choose Bluetooth Low Energy!) but what if you want to send data very far? Most WiFi, Bluetooth, Zigbee and other wireless chipsets use 2.4GHz, which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
  CR123 battery holder: CR123 Battery Holder
  ESP32 UWB v1.0: Makerfabs ESP32 UWB module is based on DW1000, it acts like a continuously scanning radar, that precisely locks onto another device (called Anchor) and communicates with it, thus calculating its own location.
